# Fritzing sketch at89s51 (saved by Fritzing 0.9.3b)
breadboards: 2

parts:
  Heartbeat = LED - 5mm [color="Yellow (595nm)" package="5 mm [THT]"]
  Error = LED - 5mm [color="Red (633nm)" package="5 mm [THT]"]
  Programming = LED - 5mm [color="Green (570nm)" package="5 mm [THT]"]
  R1 = Resistor [tolerance=±5% resistance=10k package=THT]
  IC1 = IC, DIP package, 40 pins [chip_label=AT89S51]
  XTAL1 = Crystal [frequency="16 Mhz" package=THT]
  Reset = Pushbutton [package="[THT]"]
  Part1 = Arduino Nano (Rev3.0) (ICSP)
  LED = LED - 5mm [color="White (4500K)" package="5 mm [THT]"]
  R2 = Resistor [tolerance=±5% resistance=10k package=THT]
  C2 = Capacitor [part_number=22pF package=cap-pth-small2]
  C3 = Capacitor [part_number=22pF package=cap-pth-small2]

nets:
  N1: Heartbeat.cathode, Error.cathode, Programming.cathode, R1.Pin_1
  N2: Heartbeat.anode, Part1.D9
  N3: Error.anode, Part1.D8
  N4: Programming.anode, Part1.D7
  N5: R1.Pin_0, IC1.pin20, Part1.GND, R2.Pin_0, C2.2, C3.1
  N6: IC1.pin3, LED.anode
  N7: IC1.pin6, Part1.D11/MOSI
  N8: IC1.pin7, Part1.D12/MISO
  N9: IC1.pin8, Part1.D13/SCK
  N10: IC1.pin9, Reset.Pin_3, Reset.Pin_4, Part1.D10
  N11: IC1.pin18, XTAL1.pin_0, C3.2
  N12: IC1.pin19, XTAL1.pin_1, C2.1
  N13: IC1.pin31, IC1.pin40, Reset.Pin_1, Reset.Pin_2, Part1.5V
  N14: LED.cathode, R2.Pin_1

custom parts:
  Capacitor: Capacitor Standard 0603 ceramic capacitor, and 0.1 leaded capacitor.
