# Fritzing sketch stc89c51rc (saved by Fritzing 0.9.3b)
breadboards: 1

parts:
  XTAL1 = Crystal [frequency="16 Mhz" package=THT]
  USB_to_Serial/TTL_Adapter = USB TTL Serial Cable
  Resistor = Resistor [tolerance=±5% resistance=10k package=THT]
  Reset = Pushbutton [package="[THT]"]
  IC1 = IC, DIP package, 40 pins [chip_label=STC89C51RC]
  LED = LED - 5mm [color="White (4500K)" package="5 mm [THT]"]
  C3 = Capacitor [part_number=22pF package=cap-pth-small2]
  C4 = Capacitor [part_number=22pF package=cap-pth-small2]

nets:
  N1: XTAL1.pin_0, IC1.pin18, C3.2
  N2: XTAL1.pin_1, IC1.pin19, C4.1
  N3: USB_to_Serial/TTL_Adapter.RX, IC1.pin11
  N4: USB_to_Serial/TTL_Adapter.TX, IC1.pin10
  N5: USB_to_Serial/TTL_Adapter.5V, Reset.Pin_1, Reset.Pin_2, IC1.pin40
  N6: USB_to_Serial/TTL_Adapter.GND, IC1.pin20, LED.cathode, C3.1, C4.2
  N7: Resistor.Pin_0, LED.anode
  N8: Resistor.Pin_1, IC1.pin3
  N9: Reset.Pin_3, Reset.Pin_4, IC1.pin9

custom parts:
  Capacitor: Capacitor Standard 0603 ceramic capacitor, and 0.1 leaded capacitor.
